// Logisim project GCore.circ as structural Verilog: 7 circuits, main circuit main
module mem_control (
  input  [3:0] addr,
  input  [7:0] writedata,
  input  write,
  input  read,
  input  clk,
  input  rst,
  output [7:0] data
);

  RAM #(.addrWidth(4), .bus("separate")) ram_1 (
    .addr(addr), .din(writedata), .data(data), .str(write), .sel(1'b1), .clk(clk), .ld(read), .clr(rst));
endmodule

module main (
);

  wire undriven;
  wire [7:0] alu_ans, bit_extender_1_out, mem_control_data, mux_out, opram_control_op, pc_addr,
       shifter_1_out, undriven_2;

  pc pc (.rst(undriven), .addr(pc_addr));  // open: jumpaddr, jump, clk
  opram_control opram_control (
    .addr(pc_addr), .rst(undriven), .op(opram_control_op));  // open: writeop, write, read, clk
  mem_control mem_control (
    .addr(opram_control_op[3:0]), .rst(undriven), .data(mem_control_data));  // open: writedata, write, read, clk
  assign bit_extender_1_out = {{4{1'b0}}, opram_control_op[3:0]};  // Bit_Extender bit_extender_1
  mux mux (.a(mem_control_data), .b(bit_extender_1_out), .c(alu_ans), .d(shifter_1_out), .out(mux_out));  // open: sel
  accum accum (.writedata(mux_out), .rst(undriven), .data(undriven_2));  // open: write, clk
  alu alu (.b(mem_control_data), .a(undriven_2), .ans(alu_ans));  // open: aluop, clk, zero
  Shifter shifter_1 (.in(undriven_2), .\dist (3'b100), .out(shifter_1_out));
endmodule

module pc (
  input  [7:0] jumpaddr,
  input  jump,
  input  clk,
  input  rst,
  output [7:0] addr
);

  wire [7:0] adder_1_out, multiplexer_1_out;

  Adder adder_1 (.a(addr), .b(8'h1), .out(adder_1_out));  // open: cin, cout
  Multiplexer #(.width(8), .enable("false")) multiplexer_1 (
    .in0(adder_1_out), .in1(jumpaddr), .out(multiplexer_1_out), .sel(jump));
  Register Mem (.D(multiplexer_1_out), .en(1'b1), .Q(addr), .clk(clk), .clr(rst));
endmodule

module opram_control (
  input  [7:0] addr,
  input  [7:0] writeop,
  input  write,
  input  read,
  input  clk,
  input  rst,
  output [7:0] op
);

  wire and_1_out, not_1_out;

  not not_1 (not_1_out, write);
  and and_1 (and_1_out, not_1_out, read);
  RAM #(.bus("separate")) ram_1 (
    .addr(addr), .din(writeop), .data(op), .str(write), .sel(1'b1), .clk(clk), .ld(and_1_out), .clr(rst));
endmodule

module mux (
  input  [7:0] a,
  input  [7:0] b,
  input  [7:0] c,
  input  [7:0] d,
  input  [1:0] sel,
  output [7:0] out
);

  Multiplexer #(.select(2), .width(8), .enable("false")) multiplexer_1 (
    .in0(a), .in1(b), .in2(c), .in3(d), .out(out), .sel(sel));
endmodule

module accum (
  input  [7:0] writedata,
  input  [7:0] data,
  input  write,
  input  clk,
  input  rst
);

  wire [7:0] Mem_q, multiplexer_1_out, multiplexer_2_out;

  Multiplexer #(.width(8), .enable("false")) multiplexer_1 (
    .in0(Mem_q), .in1(writedata), .out(multiplexer_1_out), .sel(write));
  Multiplexer #(.width(8), .enable("false")) multiplexer_2 (
    .in0(multiplexer_1_out), .in1({8{1'b0}}), .out(multiplexer_2_out), .sel(rst));
  Register Mem (.D(multiplexer_2_out), .en(1'b1), .Q(Mem_q), .clk(clk), .clr(1'b0));
  assign data = Mem_q;  // Buffer buffer_1, 8 bits wide
endmodule

module alu (
  input  [7:0] b,
  input  [7:0] a,
  input  [2:0] aluop,
  input  clk,
  output zero,
  output [7:0] ans
);

  wire [0:0] comparator_1_lt, comparator_2_eq;
  wire [7:0] adder_1_out, and_1_out, multiplexer_1_out, or_1_out, subtractor_1_out, xor_1_out;

  Adder adder_1 (.a(a), .b(b), .out(adder_1_out));  // open: cin, cout
  Subtractor subtractor_1 (.a(a), .b(b), .out(subtractor_1_out));  // open: bin, bout
  assign and_1_out = a & b;  // AND_Gate and_1, 8 bits wide
  assign or_1_out = a | b;  // OR_Gate or_1, 8 bits wide
  assign xor_1_out = a ^ b;  // XOR_Gate xor_1, 8 bits wide
  Comparator comparator_1 (.a(a), .b(b), .lt(comparator_1_lt[0]));  // open: gt, eq
  Comparator comparator_2 (.a(a), .b(b), .eq(comparator_2_eq[0]));  // open: gt, lt
  Multiplexer #(.select(3), .width(8), .enable("false")) multiplexer_1 (
    .in0(adder_1_out), .in1(subtractor_1_out), .in2(and_1_out), .in3(or_1_out), .in4(xor_1_out),
    .in5({8{1'b0}}), .in6({{7{1'b0}}, comparator_1_lt[0]}), .in7({{7{1'b0}}, comparator_2_eq[0]}),
    .out(multiplexer_1_out), .sel(aluop));
  Register Mem (.D(multiplexer_1_out), .en(1'b1), .Q(ans), .clk(clk), .clr(1'b0));

  assign zero = ans[0];
endmodule
